// Logisim project bf.circ as structural Verilog: 1 circuit, main circuit main
module main (
  output out_1,
  output out_2,
  output out_3,
  output out_4
);

  wire clock_1_out;
  wire [2:0] rom_1_data;
  wire [7:0] counter_1_q, ram_1_dout, register_1_q, subtractor_1_out;

  Counter counter_1 (.clk(clock_1_out), .Q(counter_1_q));  // open: clr, load, up, count, D, carry
  Clock clock_1 (.out(clock_1_out));
  RAM ram_1 (.addr(subtractor_1_out), .we(out_1), .clk(clock_1_out), .dout(ram_1_dout));  // open: oe, din
  ROM #(.dataWidth(3)) rom_1 (.addr(counter_1_q), .data(rom_1_data));
  Register register_1 (.D(subtractor_1_out), .en(1'b1), .clk(out_1), .Q(register_1_q));  // open: clr
  Demultiplexer #(.select(3)) demultiplexer_1 (
    .out0(out_1), .out1(out_2), .out2(out_3), .out3(out_4), .in(1'b1), .sel(rom_1_data));  // open: out4, out5, out6, out7
  Subtractor subtractor_1 (.a(register_1_q), .b(8'h1), .out(subtractor_1_out));  // open: bin, bout
  Adder adder_1 (.a(register_1_q), .b(8'h1), .out(subtractor_1_out));  // open: cin, cout

  // Notes on the sheet:
  //   contents of rom_1 (hex, n*v repeats v):
  //   1 2 2 2 4
endmodule
